# Fritzing sketch Equalizer (saved by Fritzing 0.9.3b)
breadboards: 1

parts:
  Parça2 = Arduino Uno (Rev3)
  FC-2 = Sound Sensor
  LED14 = smd LED [color="Red (633nm)" package="1206 [SMD]"]
  LED15 = smd LED [color="Red (633nm)" package="1206 [SMD]"]
  LED16 = smd LED [color="Red (633nm)" package="1206 [SMD]"]
  LED17 = smd LED [color="Red (633nm)" package="1206 [SMD]"]
  LED18 = smd LED [color="Red (633nm)" package="1206 [SMD]"]
  LED19 = smd LED [color="Red (633nm)" package="1206 [SMD]"]
  LED20 = smd LED [color="Red (633nm)" package="1206 [SMD]"]
  LED21 = smd LED [color="Red (633nm)" package="1206 [SMD]"]
  LED22 = smd LED [color="Red (633nm)" package="1206 [SMD]"]
  LED23 = smd LED [color="Red (633nm)" package="1206 [SMD]"]
  LED24 = smd LED [color="Red (633nm)" package="1206 [SMD]"]
  LED25 = smd LED [color="Red (633nm)" package="1206 [SMD]"]
  R1 = Resistor [tolerance=±5% resistance=220 package="0805 [SMD]"]
  R2 = Resistor [tolerance=±5% resistance=220 package="0805 [SMD]"]
  R3 = Resistor [tolerance=±5% resistance=220 package="0805 [SMD]"]
  R4 = Resistor [tolerance=±5% resistance=220 package="0805 [SMD]"]
  R5 = Resistor [tolerance=±5% resistance=220 package="0805 [SMD]"]
  R6 = Resistor [tolerance=±5% resistance=220 package="0805 [SMD]"]
  R7 = Resistor [tolerance=±5% resistance=220 package="0805 [SMD]"]
  R8 = Resistor [tolerance=±5% resistance=220 package="0805 [SMD]"]
  R9 = Resistor [tolerance=±5% resistance=220 package="0805 [SMD]"]
  R10 = Resistor [tolerance=±5% resistance=220 package="0805 [SMD]"]
  R11 = Resistor [tolerance=±5% resistance=220 package="0805 [SMD]"]
  R12 = Resistor [tolerance=±5% resistance=220 package="0805 [SMD]"]

nets:
  N1: Parça2.A0, FC-2.OUT
  N2: Parça2.D8, Parça2.D9_PWM, Parça2.D10_PWM/SS, Parça2.D11_PWM/MOSI, Parça2.D12/MISO, Parça2.D13/SCK, Parça2.D2, Parça2.D3_PWM, Parça2.D4, Parça2.D5_PWM, Parça2.D6_PWM, Parça2.D7, FC-2.GND, LED14.cathode, LED15.cathode, LED16.cathode, LED17.cathode, LED18.cathode, LED19.cathode, LED20.cathode, LED21.cathode, LED22.cathode, LED23.cathode, LED24.cathode, LED25.cathode
  5V: Parça2.5V, FC-2.VCC
  N3: LED14.anode, R12.Pin_0
  N4: LED15.anode, R1.Pin_0
  N5: LED16.anode, R10.Pin_0
  N6: LED17.anode, R5.Pin_0
  N7: LED18.anode, R3.Pin_0
  N8: LED19.anode, R6.Pin_0
  N9: LED20.anode, R2.Pin_0
  N10: LED21.anode, R4.Pin_0
  N11: LED22.anode, R9.Pin_0
  N12: LED23.anode, R7.Pin_0
  N13: LED24.anode, R8.Pin_0
  N14: LED25.anode, R11.Pin_0
